// Logisim project And3Way.circ as structural Verilog: 1 circuit, main circuit main
module main (
  input  A,
  input  B,
  input  C,
  output out_4
);

  wire and_1_out, and_2_out;

  and and_1 (and_1_out, A, B);
  and and_2 (and_2_out, and_1_out, C);
  and and_3 (out_4, and_2_out, B);
endmodule
