// Logisim project And4Way.circ as structural Verilog: 1 circuit, main circuit main
module main (
  input  [3:0] in_1,
  output out_2
);

  and and_1 (out_2, in_1[1], in_1[0], in_1[2], in_1[3]);
endmodule
