// Logisim project And5Way.circ as structural Verilog: 1 circuit, main circuit main
module main (
  input  a,
  input  b,
  input  c,
  input  d,
  input  e,
  input  f,
  output out_7
);

  wire and_1_out, and_2_out, and_3_out, and_4_out;

  and and_1 (and_1_out, a, b);
  and and_2 (and_2_out, and_1_out, c);
  and and_3 (and_3_out, and_2_out, d);
  and and_4 (and_4_out, and_3_out, e);
  and and_5 (out_7, and_4_out, f);
endmodule
