// Logisim project Or3Way.circ as structural Verilog: 1 circuit, main circuit main
module main (
  input  [2:0] in_1,
  output out_2
);

  or or_1 (out_2, in_1[0], in_1[1], in_1[2]);
endmodule
