// Logisim project Or6Way.circ as structural Verilog: 1 circuit, main circuit main
module main (
  input  a,
  input  b,
  input  c,
  input  d,
  input  e,
  input  f,
  output out_7
);

  wire or_1_out, or_2_out, or_3_out, or_4_out, or_5_out;

  or or_1 (or_1_out, a, b);
  or or_2 (or_2_out, or_1_out, c);
  or or_3 (or_3_out, or_2_out, d);
  or or_4 (or_4_out, or_3_out, e);
  or or_5 (or_5_out, or_4_out, f);
  or or_6 (out_7, or_5_out, a);
endmodule
